// Digital circuit SUBLEQ24.dig as structural Verilog
module SUBLEQ24 (
  input  XTAL,
  input  TRACE,
  input  TRACECLK,
  input  _16xBaudClk
);

  wire _74ls163_1_q0, _74ls163_1_q1, _74ls163_1_q2, _74ls163_1_q3, _74ls163_1_tc, _74ls238_1_y0,
       _74ls238_1_y1, _74ls238_1_y2, _74ls238_1_y3, _74ls238_1_y4, _74ls238_1_y5, _74ls238_1_y6,
       _74ls238_2_y0, _74ls238_2_y1, _74ls238_2_y2, _74ls238_2_y3, _74ls238_2_y4, _74ls238_2_y5,
       _74ls238_2_y6, _74ls238_2_y7, Aaddr_CK, and_1_out, and_3_out, and_4_out, and_5_out, and_7_out,
       and_8_out, and_9_out, and_11_out, Aval_CK, Baddr_CK, Bval_CK, delay_1_out, delay_2_out, delay_3_out,
       half7474_1_q, half7474_2_q, half7474_3_q, half7474_4_nq, half7474_5_nq, half7474_6_nq, half7474_7_nq,
       half7474_7_q, half7474_8_q, half7474_9_q, half7474_10_q, IO_RX, IO_TX, IORCYCLE, IOWCYCLE, LEQ, M_out,
       nAaddr_E, nand_1_out, nand_2_out, nand_3_out, nBaddr_E, nE_PC, nIORCYCLE, nIOWCYCLE, not_1_out,
       not_7_out, not_9_out, not_13_out, not_14_out, not_15_out, not_16_out, not_17_out, not_18_out,
       not_19_out, nPC_LD, nR, nRD, nResult_E, nWR, nXTAL, oneshot_1_o, or_2_out, or_4_out, or_5_out,
       or_7_out, or_8_out, or_10_out, or_11_out, PC_CK, PC_FLASH, PC_RESET, programcounter_1_p8,
       pulldown_2_out, R_out, register_1_io, register_2_io, Res2, Res3, reset_1_out, reset_2_out,
       RESET_FLASH_out, RESET_RAM_out, S_out, T0, T2, T4, T6, T8, T9, T10, T11, T12, T13, T14, T15, UART_RD,
       uart_telnet_gw_1_tx, uartrx_1_rdy, uarttx_1_tx;
  wire [7:0] subtractor_1_q;
  wire [15:0] subtractor_1_q_2;
  wire [23:0] AA, AV, BA, BV, register_1_addr, register_1_value, register_2_value, subtractor_1_spy;

  and and_1 (and_1_out, register_1_io, T6);
  and and_2 (IO_RX, register_2_io, T2);
  // Probe on IO_TX
  // Probe on and_1_out
  UartTx uarttx_1 (.nD(subtractor_1_q), .STB(IO_TX), .CLK(_16xBaudClk), .TX(uarttx_1_tx));  // open: BSY
  RS_FF_AS rs_ff_as_1 (.S(and_1_out), .R(T0), .Q(IOWCYCLE), .nQ(nIOWCYCLE));
  RS_FF_AS rs_ff_as_2 (.S(IO_RX), .R(T15), .Q(IORCYCLE), .nQ(nIORCYCLE));
  not not_1 (not_1_out, T15);
  // Probe on nIOWCYCLE
  _74LS238 _74ls238_1 (
    .A(register_1_addr[0]), .B(register_1_addr[1]), .C(register_1_addr[2]), .G(and_1_out), .nGA(1'b0),
    .nGB(1'b0), .Y0(_74ls238_1_y0), .Y1(_74ls238_1_y1), .Y2(_74ls238_1_y2), .Y3(_74ls238_1_y3),
    .Y4(_74ls238_1_y4), .Y5(_74ls238_1_y5), .Y6(_74ls238_1_y6), .Y7(IO_TX));
  // Probe on nIORCYCLE
  _74LS238 _74ls238_2 (
    .A(register_1_addr[0]), .B(register_1_addr[1]), .C(register_1_addr[2]), .G(IO_RX), .nGA(1'b0),
    .nGB(1'b0), .Y0(_74ls238_2_y0), .Y1(_74ls238_2_y1), .Y2(_74ls238_2_y2), .Y3(_74ls238_2_y3),
    .Y4(_74ls238_2_y4), .Y5(_74ls238_2_y5), .Y6(_74ls238_2_y6), .Y7(_74ls238_2_y7));
  Reset #(.invertOutput("false")) reset_1 (.out(reset_1_out));
  Uart_Telnet_GW uart_telnet_gw_1 (.RX(uarttx_1_tx), .CLK(_16xBaudClk), .TX(uart_telnet_gw_1_tx));
  Half7474 half7474_1 (.nSD(nand_2_out), .D(1'b0), .CP(nR), .nRD(not_1_out), .Q(half7474_1_q));  // open: nQ
  and and_3 (and_3_out, nResult_E, nIOWCYCLE);
  and and_4 (and_4_out, nIOWCYCLE, nIORCYCLE);
  // Probe on _74ls238_1_y0
  // Probe on _74ls238_1_y1
  // Probe on _74ls238_1_y2
  // Probe on _74ls238_1_y3
  // Probe on _74ls238_1_y4
  // Probe on _74ls238_1_y5
  // Probe on _74ls238_1_y6
  // Probe on IO_TX
  // Probe on _74ls238_2_y0
  // Probe on _74ls238_2_y1
  // Probe on _74ls238_2_y2
  // Probe on _74ls238_2_y3
  // Probe on _74ls238_2_y4
  // Probe on _74ls238_2_y5
  // Probe on _74ls238_2_y6
  // Probe on _74ls238_2_y7
  nand nand_1 (nand_1_out, half7474_1_q, T15);
  Register register_1 (
    .D({subtractor_1_q_2, subtractor_1_q}), .CLKaddr(Baddr_CK), .CLKval(Bval_CK), .nOEaddr(nBaddr_E),
    .nOEval(register_1_io), .Addr(register_1_addr), .Value(register_1_value), .IO(register_1_io), .SpyA(BA),
    .SpyV(BV));
  Subtractor subtractor_1 (
    .B(register_1_value), .nOE(and_3_out), .nCY(and_4_out), .A(register_2_value),
    .Q({subtractor_1_q_2, subtractor_1_q}), .LEQ(LEQ), .Spy(subtractor_1_spy));
  Register register_2 (
    .D({subtractor_1_q_2, subtractor_1_q}), .CLKaddr(Aaddr_CK), .CLKval(Aval_CK), .nOEaddr(nAaddr_E),
    .nOEval(1'b0), .Addr(register_1_addr), .Value(register_2_value), .IO(register_2_io), .SpyA(AV), .SpyV(AA));
  // ProgramCounter programcounter_1: pin names not known; wires that end beside it: {subtractor_1_q_2, subtractor_1_q}, PC_CK, nPC_LD, nE_PC, PC_RESET, PC_FLASH, register_1_addr, programcounter_1_p8
  UartRx uartrx_1 (
    .RX(uart_telnet_gw_1_tx), .nACK(nand_1_out), .nOE(nand_2_out), .CLK(_16xBaudClk), .nQ(subtractor_1_q),
    .RDY(uartrx_1_rdy));
  nand nand_2 (nand_2_out, UART_RD, uartrx_1_rdy);
  // Probe on register_1_value
  // Probe on subtractor_1_spy
  // Probe on register_2_value
  RAMSinglePortSel #(.AddrBits(24), .isProgramMemory("true"), .Bits(24)) ramsingleportsel_1 (
    .A(register_1_addr), .CS(~reset_1_out), .WE(~nWR), .OE(~nRD), .D({subtractor_1_q_2, subtractor_1_q}));
  LED END (.in(programcounter_1_p8));
  // NotConnected on subtractor_1_q_2
  PullUp #(.Bits(24)) pullup_1 (.out({subtractor_1_q_2, subtractor_1_q}));
  PullDown #(.Bits(24)) pulldown_1 (.out(register_1_addr));
  // Probe on {subtractor_1_q_2, subtractor_1_q}
  // Probe on register_1_addr
  Button M (.out(M_out));
  Button R (.out(R_out));
  Button S (.out(S_out));
  Button RESET_FLASH (.out(RESET_FLASH_out));
  Button RESET_RAM (.out(RESET_RAM_out));
  and and_5 (and_5_out, TRACECLK, TRACE);
  or or_1 (PC_FLASH, reset_2_out, RESET_FLASH_out);
  Reset #(.invertOutput("false")) reset_2 (.out(reset_2_out));
  and and_6 (UART_RD, IORCYCLE, T2);
  or or_2 (or_2_out, Aval_CK, T2);
  or or_3 (PC_CK, Aaddr_CK, Baddr_CK, T14, Res3);
  or or_4 (or_4_out, T0, Aaddr_CK, T4, Baddr_CK, T13);
  or or_5 (or_5_out, R_out, S_out, and_5_out);
  not not_2 (nXTAL, XTAL);
  and and_7 (and_7_out, or_2_out, nIORCYCLE);
  not not_3 (nE_PC, or_4_out);
  Half7474 half7474_2 (.nSD(1'b1), .D(R_out), .CP(XTAL), .nRD(nR), .Q(half7474_2_q));  // open: nQ
  Half7474 half7474_3 (.nSD(1'b1), .D(or_5_out), .CP(XTAL), .nRD(nR), .Q(half7474_3_q));  // open: nQ
  or or_6 (PC_RESET, PC_FLASH, RESET_RAM_out);
  not not_4 (nAaddr_E, and_7_out);
  OneShot oneshot_1 (.i(pulldown_2_out), .o(oneshot_1_o));
  PullDown pulldown_2 (.out(pulldown_2_out));
  Half7474 half7474_4 (.nSD(1'b1), .D(half7474_2_q), .CP(XTAL), .nRD(nR), .nQ(half7474_4_nq));  // open: Q
  Half7474 half7474_5 (.nSD(1'b1), .D(half7474_3_q), .CP(XTAL), .nRD(nR), .nQ(half7474_5_nq));  // open: Q
  not not_5 (nR, delay_1_out);
  Delay #(.delayTime(10)) delay_1 (.in(PC_RESET), .out(delay_1_out));
  not not_6 (nWR, T9);
  not not_7 (not_7_out, nIOWCYCLE);
  or or_7 (or_7_out, oneshot_1_o, and_8_out);
  and and_8 (and_8_out, half7474_2_q, half7474_4_nq);
  and and_9 (and_9_out, half7474_3_q, half7474_5_nq);
  Delay #(.delayTime(10)) delay_2 (.in(nR), .out(delay_2_out));
  nand nand_3 (nand_3_out, nIOWCYCLE, LEQ, T13);
  or or_8 (or_8_out, T10, T9, T8, Bval_CK, T6);
  not not_8 (nResult_E, T9);
  not not_9 (not_9_out, and_9_out);
  Half7474 half7474_6 (.nSD(nR), .D(T15), .CP(XTAL), .nRD(1'b1), .nQ(half7474_6_nq));  // open: Q
  not not_10 (Res2, delay_2_out);
  and and_10 (nPC_LD, nand_3_out, nR);
  or or_9 (nRD, IO_RX, not_7_out, T9);
  Half7474 half7474_7 (.nSD(1'b1), .D(half7474_7_nq), .CP(or_7_out), .nRD(nR), .Q(half7474_7_q), .nQ(half7474_7_nq));
  Half7474 half7474_8 (.nSD(not_9_out), .D(1'b0), .CP(1'b0), .nRD(half7474_6_nq), .Q(half7474_8_q));  // open: nQ
  Delay #(.delayTime(20)) delay_3 (.in(nR), .out(delay_3_out));
  not not_11 (nBaddr_E, or_8_out);
  or or_10 (or_10_out, half7474_7_q, half7474_8_q);
  // Probe on half7474_8_q
  not not_12 (Res3, delay_3_out);
  // Probe on M_out
  Half7474 half7474_9 (.nSD(1'b1), .D(M_out), .CP(nXTAL), .nRD(nR), .Q(half7474_9_q));  // open: nQ
  Half7474 half7474_10 (.nSD(1'b1), .D(or_10_out), .CP(nXTAL), .nRD(nR), .Q(half7474_10_q));  // open: nQ
  not not_13 (not_13_out, nRD);
  not not_14 (not_14_out, nWR);
  LED led_1 (.in(Aaddr_CK));
  LED led_2 (.in(not_15_out));
  not not_15 (not_15_out, nAaddr_E);
  LED led_3 (.in(Aval_CK));
  // Probe on half7474_9_q
  LED RUN (.in(half7474_10_q));
  // Probe on half7474_10_q
  LED led_4 (.in(not_13_out));
  LED led_5 (.in(not_14_out));
  and and_11 (and_11_out, half7474_10_q, XTAL);
  // Probe on AA
  // Probe on BA
  or or_11 (or_11_out, half7474_9_q, Res2, and_11_out);
  // Probe on and_11_out
  not not_16 (not_16_out, nPC_LD);
  not not_17 (not_17_out, nE_PC);
  not not_18 (not_18_out, nBaddr_E);
  LED led_6 (.in(PC_CK));
  LED led_7 (.in(not_16_out));
  LED led_8 (.in(not_17_out));
  LED led_9 (.in(Baddr_CK));
  LED led_10 (.in(not_18_out));
  LED led_11 (.in(Bval_CK));
  LED CLOCK (.in(or_11_out));
  // Probe on or_11_out
  _74LS163 _74ls163_1 (
    .nPE(nR), .nSR(1'b1), .CP(or_11_out), .CET(1'b1), .CEP(1'b1), .P0(1'b0), .P1(1'b0), .P2(1'b0), .P3(1'b0),
    .TC(_74ls163_1_tc), .Q0(_74ls163_1_q0), .Q1(_74ls163_1_q1), .Q2(_74ls163_1_q2), .Q3(_74ls163_1_q3));
  _74LS238 _74ls238_3 (
    .A(_74ls163_1_q0), .B(_74ls163_1_q1), .C(_74ls163_1_q2), .G(1'b1), .nGA(_74ls163_1_q3), .nGB(1'b0),
    .Y0(T0), .Y1(Aaddr_CK), .Y2(T2), .Y3(Aval_CK), .Y4(T4), .Y5(Baddr_CK), .Y6(T6), .Y7(Bval_CK));
  _74LS238 _74ls238_4 (
    .A(_74ls163_1_q0), .B(_74ls163_1_q1), .C(_74ls163_1_q2), .G(_74ls163_1_q3), .nGA(1'b0), .nGB(1'b0),
    .Y0(T8), .Y1(T9), .Y2(T10), .Y3(T11), .Y4(T12), .Y5(T13), .Y6(T14), .Y7(T15));
  // Probe on AV
  // Probe on BV
  not not_19 (not_19_out, nResult_E);
  // Probe on _74ls163_1_tc
  // Probe on AV
  // Probe on BV
  LED led_12 (.in(LEQ));
  LED led_13 (.in(not_19_out));

  // Other names for the same wires on the sheet: BAUD = _16xBaudClk; nRes1 = nR; T1 = Aaddr_CK; T3 = Aval_CK;
  //   T5 = Baddr_CK; T7 = Bval_CK

  // Notes on the sheet:
  //   XTAL: Hz: 16000
  //   TRACECLK: Hz: 80
  //   _16xBaudClk: Hz: 500000
  //   REGISTER-B
  //   REGISTER-A
  //   UART
  //   MEMORY
  //   PROGRAM COUNTER
  //   SUBTRACTOR
  //   DATA BUS
  //   ADDRESS BUS
  //   MICROSTEP
  //   RUN/HALT
  //   STEP
  //   if(a < 0) mem[b] += (int)getchar(); /* input */
  //           else if(b < 0) printf("%c", (char)mem[a]); /* output */
  //   stty -icanon -echo && nc localhost 23
  //   PROTO-CONTROL/SEQUENCER
  //   PROTO-MICROCODE
  //   Reg A
  //   Reg B
  //   MEM
  //   READ
  //   MEM
  //   WRITE
  //   LOAD A
  //   ADDR
  //   A→
  //   ADDR
  //   LOAD A
  //   VALUE
  //   UART RX:
  //   1 x '595
  //   1 x '393
  //   1 x '74
  //   0.66 x '04
  //   0.5 x '00
  //   ADDRESS
  //   UART TX:
  //   2 x '165
  //   1 x '393
  //   1 x '74
  //   0.75 x '04
  //   1 x '00
  //   PC
  //   INCR
  //   PC
  //   LOAD
  //   PC→
  //   ADDR
  //   LOAD B
  //   ADDR
  //   B→
  //   ADDR
  //   LOAD B
  //   VALUE
  //   VALUE
  //   UART MISC:
  //   0.5 x '74
  //   0.16 x '04
  //   0.5 x '00
  //   LEQ
  //   SUB→
  //   DATA
  //   T0
  //   ........Output PC+0 to Address bus
  //   ........RAM outputs A-address to Data bus
  //   T1
  //   ........Latch A-address into register
  //   ........Increment PC
  //   ........Output PC+1to Address bus
  //   ........(RAM outputs address of B to Data bus)
  //   T2
  //   ........A-address register output to Address bus
  //   ........RAM outputs value of data poited to by A to Data bus
  //   T3
  //   ........A-address register output to Address bus
  //   ........RAM outputs value of [A] to Data bus
  //   ........Latch value of [A] into A value register
  //   T4
  //   ........Output PC+1 to Address bus
  //   ........RAM outputs address of B to Data bus
  //   T5
  //   ........Latch B-address into register
  //   ........Increment PC
  //   ........(Output PC+2 to Address bus)
  //   ........(RAM outputs B-address to Data bus)
  //   T6
  //   ........B-address register output to Address bus
  //   ........RAM outputs value [B] to Data bus
  //   T7
  //   ........B-address register output to Address bus
  //   ........RAM outputs value of [B] to Data bus
  //   ........Latch value of [B] into B value register
  //   T8
  //   ........B-address register output to Address bus
  //   ........RAM outputs value of [B] to Data bus
  //   T9
  //   ........B-address register output to Address bus
  //   ........Subtractor output [B]-[A] to Data bus
  //   ........Write subtaction result into RAM pointef to B-address
  //   T10
  //   ........B-address register output to Address bus
  //   ........RAM outputs value of [B] to Data bus
  //   T11
  //   ........RAM outputs value of <random HiZ> to Data bus
  //   T12
  //   ........RAM outputs value of <random HiZ> to Data bus
  //   T13
  //   ........Output PC+2 to Address bus
  //   ........RAM outputs [C] to Data bus
  //   T14 (not LEQ)
  //   ........Increment PC
  //   ........(Output PC+3 (next instruction) to Address bus)
  //   ........(RAM outputs A-address to Data bus)
  //   T14 (LEQ)
  //   ........Load PC with [C] from Data bus
  //   ........
  //   T15
  //   ........(Output PC+3 (next instruction) to Address bus
  //   ........(RAM outputs value of (next instruction) A-address to Data bus)
endmodule
