// Digital circuit Uart_Telnet_GW.dig as structural Verilog
module Uart_Telnet_GW (
  input  RX,
  input  CLK,
  output TX
);

  wire delay_1_out, delay_2_out, delay_3_out, not_1_out, or_1_out, or_2_out, reset_1_out, telnet_1_av,
       uartrx_1_rdy;
  wire [7:0] not_2_out, telnet_1_out, uartrx_1_nq;

  UartRx uartrx_1 (.RX(RX), .nACK(not_1_out), .nOE(1'b0), .CLK(CLK), .nQ(uartrx_1_nq), .RDY(uartrx_1_rdy));
  not not_1 (not_1_out, delay_1_out);
  Delay #(.delayTime(20)) delay_1 (.in(uartrx_1_rdy), .out(delay_1_out));
  assign not_2_out = ~uartrx_1_nq;  // Not not_2, 8 bits wide
  Delay #(.delayTime(10)) delay_2 (.in(or_1_out), .out(delay_2_out));
  or or_1 (or_1_out, delay_3_out, uartrx_1_rdy);
  PullDown pulldown_1 (.out(delay_2_out));
  PullDown pulldown_2 (.out(uartrx_1_rdy));
  Telnet #(.telnetEscape("false")) telnet_1 (
    .in(not_2_out), .C(delay_2_out), .wr(uartrx_1_rdy), .rd(telnet_1_av), .out(telnet_1_out), .av(telnet_1_av));
  PullDown pulldown_3 (.out(telnet_1_av));
  Delay #(.delayTime(5)) delay_3 (.in(telnet_1_av), .out(delay_3_out));
  // Probe on delay_3_out
  // Probe on telnet_1_out
  or or_2 (or_2_out, delay_3_out, reset_1_out);
  Reset #(.invertOutput("false")) reset_1 (.out(reset_1_out));
  UartTx uarttx_1 (.nD(telnet_1_out), .STB(or_2_out), .CLK(CLK), .TX(TX));  // open: BSY
  // Probe on TX

  // Notes on the sheet:
  //   CLK: Hz: 1000
  //   SERIAL -> TELNET GATEWAY
  //   ONLY FOR TESTING IN SIMULATION
endmodule
